# Fritzing sketch schema (saved by Fritzing 0.9.3b)

parts:
  WeMos_D1_Mini1 = WeMos D1 Mini
  Part1 = Arduino Uno (Rev3)
  J1 = Power Jack [package=power_jack_slot]
  J2 = Power Jack [package=power_jack_slot]
  Part2 = Soil Moisture Sensor
  Part3 = Soil Moisture Sensor
  Part4 = Soil Moisture Sensor
  4_Channel_Relay1 = 4 Channel Power Relay
  Part5 = BH1750 digital light sensor
  HC-SR04_Sensor_1 = HC-SR04 Ultrasonic Distance Sensor
  DHT11_1 = DHT11 module

nets:
  N1: WeMos_D1_Mini1.RX, Part1.D1/TX
  N2: WeMos_D1_Mini1.TX, Part1.D0/RX
  N3: Part1.A1, Part2.SIG
  N4: Part1.A2, Part3.SIG
  N5: Part1.A3, Part4.SIG
  N6: Part1.A4/SDA, Part5.SDA
  N7: Part1.A5/SCL, Part5.SCL
  N8: Part1.D8, 4_Channel_Relay1.IN4
  N9: Part1.D9_PWM, 4_Channel_Relay1.IN3
  N10: Part1.D10_PWM/SS, 4_Channel_Relay1.IN2
  N11: Part1.D11_PWM/MOSI, 4_Channel_Relay1.IN1
  N12: Part1.D2, HC-SR04_Sensor_1.ECHO
  N13: Part1.D3_PWM, HC-SR04_Sensor_1.TRIG
  N14: Part1.D5_PWM, DHT11_1.DATA
  N15: Part1.5V, J2.PWR
  N16: J1.GNDBREAK, J2.GNDBREAK, J2.GND
  N17: J1.PWR, 4_Channel_Relay1.COM#17

notes:
  5V
  12v
  PUMP
  VALVE
  Temperature and Humidity Sensor
  Water Level Sensor
  Communication Module
  Light Sensor
  Soil Moisture Sensor
  Power Supply

custom parts:
  4 Channel Power Relay: A 4 channel power relay. The module operates at 5V.
  BH1750 digital light sensor: BH1750 digital light sensor SKU: 101222
  DHT11 module: DHT11 black pcb module
